# Fritzing sketch pensieve (saved by Fritzing 0.9.4)
breadboards: 1

parts:
  Part1 = Adafruit T-Cobbler Plus [part_number="Adafruit #1989 and #2028"]
  ADC1 = MCP3008 [package=dil16]
  Water_Level_Sensor = Water Level Sensor

nets:
  N1: Part1.MOSI, ADC1.CH2
  N2: Part1.MISO, ADC1.CH3
  N3: Part1.SCLK, Part1.EEDAT, Part1.GPIO6, Part1.GPIO23, Part1.CE0, Part1.EECLK, Part1.GND, Part1.RXD, Part1.GPIO17, Part1.GPIO18, Part1.GPIO27, Part1.GPIO22, Part1.+3.3V_2, Part1.GPIO24, Part1.CE1, Part1.GPIO5, Part1.GPIO12, ADC1.CH1, ADC1.CH4
  N4: ADC1.CH0, ADC1.CH5
  N5: ADC1.CH6, ADC1.CH7
  N6: ADC1.VDD, Water_Level_Sensor.SIG

custom parts:
  Adafruit T-Cobbler Plus: The Raspberry Pi has landed on the Maker World like a 40-GPIO pinned, quad-USB ported, credit card sized bomb of DIY joy. And while you can use most of our great Model B accessories by hooking up our downgrade cable, its probably a good time to upgrade your set up and accessorize using all of the 40 pins. That's why we now carry the Assembled Adafruit Pi T-Cobbler Plus - Breakout + Cable for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
  Water Level Sensor: A water level sensor. This sensor operates at 3V to 5V. The Sig (signal) pin outputs an analogue signal that is in proportion to the amount of water in contact with the sensor.
